// Logisim project CPU.circ as structural Verilog: 1 circuit, main circuit main
module main (
);

  wire [3:0] PC_q_5;
  wire [4:0] PC_q_3, PC_q_4;
  wire [5:0] PC_q, PC_q_2, PC_q_6;

  Register #(.width(32)) PC (.Q({PC_q_6, PC_q_5, PC_q_4, PC_q_3, PC_q_2, PC_q}));  // open: D, en, clk, clr
  RAM #(.addrWidth(5), .dataWidth(32), .bus("asynch")) ram_1 ();  // open: addr, data, sel, ld, clr
  // Control_Unit_main main_1: pin names not known; wires that end beside it: PC_q_6
  // Register_File_main main_2: pin names not known
  // ALU_main main_3: pin names not known
endmodule
